# Fritzing sketch Schematics (saved by Fritzing 0.9.10b)
breadboards: 1

parts:
  Part1 = Arduino Nano (Rev3.0)
  R1 = PHOTOCELL [package=photocell]
  R2 = Resistor [tolerance=±5% resistance=10000 package="0805 [SMD]"]
  S1 = Pushbutton [package="[SMD]"]
  R3 = Resistor [tolerance=±5% resistance=10000 package="0805 [SMD]"]
  J1 = Basic Servo

nets:
  GND: Part1.GND, R1.P$2, J1.gnd
  N1: Part1.D2, S1.Pin_3, S1.Pin_4, R3.Pin_0
  5V: Part1.5V, R2.Pin_0, S1.Pin_1, S1.Pin_2, R3.Pin_1, J1.vcc
  N2: Part1.A7, R1.P$1, R2.Pin_1
  N3: Part1.A5, J1.pulse
