# Fritzing sketch Code (saved by Fritzing 0.9.10b)
breadboards: 1

parts:
  Part1 = Arduino Uno (Rev3)
  LCD1 = LCD screen
  R1 = TRIMPOT [maximum_resistance=10kΩ knob_status=50% power=0.5W package=3386u]
  R2 = Resistor [tolerance=±5% resistance=220 package="1206 [SMD]"]
  R3 = Resistor [tolerance=±5% resistance=10000 package="1206 [SMD]"]
  R4 = PHOTOCELL [package=photocell]
  Part2 = IR Receiver Breakout [package=PCB]

nets:
  N1: Part1.A0, R3.Pin_1, R4.P$1
  N2: Part1.D11_PWM/MOSI, LCD1.E
  N3: Part1.D12/MISO, LCD1.RS
  N4: Part1.D13/SCK, Part2.GND
  N5: Part1.D2, LCD1.DB7
  N6: Part1.D3_PWM, LCD1.DB6
  N7: Part1.D4, LCD1.DB5
  N8: Part1.D5_PWM, LCD1.DB4
  5V: Part1.5V, LCD1.VDD, LCD1.LED-, R1.CCW, R2.Pin_0, R4.P$2, Part2.VCC
  GND: Part1.GND, LCD1.VSS, LCD1.R/W, R1.CW, R3.Pin_0
  N9: LCD1.V0, R1.WIPER
  N10: LCD1.LED+, R2.Pin_1
