# Fritzing sketch Schematics (saved by Fritzing 0.9.10b)
breadboards: 1

parts:
  Part1 = Arduino Uno (Rev3)
  J1 = Basic Servo
  C1 = Electrolytic Capacitor [capacitance=1µF voltage=35V package="100 mil [THT, electrolytic]"]
  VCC1 = Battery block 9V
  Keypad4x1 = Keypad Membran 4x4
  J2 = Piezo Speaker

nets:
  N1: Part1.D8, Keypad4x1.Pin2
  N2: Part1.D9_PWM, Keypad4x1.Pin1
  N3: Part1.D10_PWM/SS, J1.pulse
  N4: Part1.D11_PWM/MOSI, J2.pin2
  N5: Part1.D2, Keypad4x1.Pin8
  N6: Part1.D3_PWM, Keypad4x1.Pin7
  N7: Part1.D4, Keypad4x1.Pin6
  N8: Part1.D5_PWM, Keypad4x1.Pin5
  N9: Part1.D6_PWM, Keypad4x1.Pin4
  N10: Part1.D7, Keypad4x1.Pin3
  5V: Part1.5V, J1.vcc, C1.+
  GND: Part1.GND, J1.gnd, C1.-, VCC1.-, J2.pin1
  N11: Part1.VIN, VCC1.+

notes:
  Keypad

custom parts:
  Keypad Membran 4x4: Membrane Keypad 4x4 Matrix
